# Fritzing sketch electronic_sketch (saved by Fritzing 0.8.3b)

parts:
  Part1 = Arduino Nano (Rev3.0)
  IC1 = ILD213T [package=so08]
  IC2 = ILD213T [package=so08]
  IC3 = ILD213T [package=so08]
  IC4 = ILD213T [package=so08]
  IC5 = ILD213T [package=so08]
  IC6 = ILD213T [package=so08]
  IC7 = ILD213T [package=so08]
  IC8 = ILD213T [package=so08]
  IC9 = ILD213T [package=so08]
  IC10 = ILD213T [package=so08]
  JP2 = Header 4 [package=screwterminal-3.5mm-4_lock]
  Q1 = Basic FET N-Channel [package="TO220 [THT]"]
  R1 = Resistor [tolerance=±5% resistance=10k package=THT]

nets:
  N1: Part1.D1/TX, JP2.2
  N2: Part1.RESET, JP2.3
  N3: Part1.GND, JP2.1, Q1.source
  N4: Part1.D2, JP2.4
  N5: Part1.D3, IC9.C2
  N6: Part1.D4, IC8.C2
  N7: Part1.D5, IC7.C2
  N8: Part1.D6, IC6.C2
  N9: Part1.D7, IC5.C2
  N10: Part1.D8, IC4.C2
  N11: Part1.D9, IC3.C2
  N12: Part1.D10, IC2.C2
  N13: Part1.D11/MOSI, IC1.C2
  N14: Part1.D12/MISO, IC10.C2
  N15: Part1.D13/SCK, Q1.gate, R1.Pin_0
  N16: IC9.A1, IC10.A1
  N17: IC9.C1, Q1.drain
